// Logisim project NOT.circ as structural Verilog: 1 circuit, main circuit main
module main (
);

  wire nand_1_out, undriven, undriven_2;

  nand nand_1 (nand_1_out, undriven, undriven_2);

  // Notes on the sheet:
  //   a
  //   b
  //   OUT
endmodule
