// Logisim project OR.circ as structural Verilog: 1 circuit, main circuit main
module main (
);

  wire nand_1_out, nand_2_out, nand_3_out, nand_4_out, undriven, undriven_2;

  nand nand_1 (nand_1_out, undriven, undriven_2);
  nand nand_2 (nand_2_out, nand_1_out, undriven_2);
  nand nand_3 (nand_3_out, undriven, nand_2_out);
  nand nand_4 (nand_4_out, nand_3_out, nand_2_out);

  // Notes on the sheet:
  //   a
  //   b
  //   w0
  //   w1
  //   w2
  //   OUT
endmodule
